// Digital circuit First_Circuit_Students.dig as structural Verilog
module First_Circuit_Students (
);

  wire trafficlightcontrol_1_p1, trafficlightcontrol_1_p2, trafficlightcontrol_1_p3,
       trafficlightcontrol_1_p4, trafficlightcontrol_1_p5, trafficlightcontrol_1_p6,
       trafficlightcontrol_1_p7, trafficlightcontrol_1_p8, trafficlightcontrol_1_p9,
       trafficlightcontrol_1_p10, trafficlightcontrol_1_p11, trafficlightcontrol_1_p12;

  // TrafficLightControl #(.tlcheight(800), .carwheight(1000), .carwpedestrians(2), .carwcars(20), .tlcwidth(800), .carwwidth(1000), .carwclock("true")) trafficlightcontrol_1: pin names not known; wires that end beside it: trafficlightcontrol_1_p1, trafficlightcontrol_1_p2, trafficlightcontrol_1_p3, trafficlightcontrol_1_p4, trafficlightcontrol_1_p5, trafficlightcontrol_1_p6, trafficlightcontrol_1_p7, trafficlightcontrol_1_p8, trafficlightcontrol_1_p9, trafficlightcontrol_1_p10, trafficlightcontrol_1_p11, trafficlightcontrol_1_p12
  // First_Automata_Students first_automata_students_1: pin names not known; wires that end beside it: trafficlightcontrol_1_p9, trafficlightcontrol_1_p10, trafficlightcontrol_1_p11, trafficlightcontrol_1_p12, trafficlightcontrol_1_p8, trafficlightcontrol_1_p7, trafficlightcontrol_1_p2, trafficlightcontrol_1_p3, trafficlightcontrol_1_p1, trafficlightcontrol_1_p5, trafficlightcontrol_1_p6, trafficlightcontrol_1_p4
endmodule
