// Digital circuit First_FSM_circuit_Students.dig as structural Verilog
module First_FSM_circuit_Students (
  input  a,
  input  b,
  input  r,
  input  C,
  output fGr,
  output fR,
  output hGe,
  output hGr,
  output hR,
  output vGe,
  output vGr,
  output vR
);

  wire and_1_out, and_2_out, and_3_out, not_1_out, or_1_out;

  not not_1 (not_1_out, r);
  not not_2 (fR, fGr);
  and and_1 (and_1_out, fR, b);
  and and_2 (and_2_out, fR, a);
  and and_3 (and_3_out, fGr, not_1_out);
  or or_1 (or_1_out, and_1_out, and_2_out, and_3_out);
  D_FF Z_0_n (.D(or_1_out), .C(C), .Q(fGr));  // open: nQ
  // Probe state on fGr

  assign hGe = 1'b0;
  assign hGr = fR;
  assign hR = fGr;
  assign vGe = 1'b0;
  assign vGr = fGr;
  assign vR = fR;

  // Other names for the same wires on the sheet: Z_0_n = fGr

  // Notes on the sheet:
  //   C: Hz: 2
endmodule
