// Digital circuit TestCircuitFSM.dig as structural Verilog
module TestCircuitFSM (
  input  a,
  input  b,
  input  r,
  input  C,
  output fGr,
  output fR,
  output hGe,
  output hGr,
  output hR,
  output vGe,
  output vGr,
  output vR
);

  wire and_1_out, and_2_out, and_3_out, and_4_out, and_5_out, and_6_out, and_7_out, and_8_out, and_9_out,
       and_10_out, and_11_out, and_12_out, and_14_out, and_15_out, and_17_out, and_18_out, and_19_out,
       and_20_out, and_22_out, and_23_out, and_24_out, not_1_out, not_2_out, not_3_out, not_4_out, not_5_out,
       not_6_out, not_7_out, or_2_out, or_3_out, or_4_out, or_5_out, Z_0_n, Z_1_n, Z_2_n, Z_3_n;

  not not_1 (not_1_out, a);
  not not_2 (not_2_out, b);
  not not_3 (not_3_out, r);
  not not_4 (not_4_out, Z_3_n);
  not not_5 (not_5_out, Z_2_n);
  not not_6 (not_6_out, Z_1_n);
  not not_7 (not_7_out, Z_0_n);
  and and_1 (and_1_out, Z_0_n, Z_1_n, Z_2_n, not_3_out);
  and and_2 (and_2_out, not_7_out, Z_3_n, not_3_out);
  and and_3 (and_3_out, Z_0_n, Z_1_n, not_5_out, b, not_3_out);
  and and_4 (and_4_out, Z_0_n, Z_1_n, not_5_out, a, not_3_out);
  and and_5 (and_5_out, not_7_out, Z_2_n, not_3_out);
  and and_6 (and_6_out, not_6_out, Z_2_n, not_3_out);
  and and_7 (and_7_out, Z_0_n, not_5_out, not_4_out, not_1_out, not_2_out, not_3_out);
  and and_8 (and_8_out, Z_0_n, not_6_out, not_4_out, not_3_out);
  and and_9 (and_9_out, not_7_out, Z_1_n, not_3_out);
  and and_10 (and_10_out, not_7_out, not_6_out, not_5_out, not_4_out);
  and and_11 (and_11_out, not_7_out, not_3_out);
  and and_12 (and_12_out, Z_1_n, not_5_out, not_1_out, not_2_out, not_3_out);
  and and_13 (fGr, Z_1_n, Z_2_n);
  or or_1 (fR, not_6_out, not_5_out);
  and and_14 (and_14_out, not_7_out, not_6_out, Z_2_n);
  and and_15 (and_15_out, Z_0_n, Z_3_n);
  and and_16 (hGr, not_5_out, not_4_out);
  and and_17 (and_17_out, Z_0_n, Z_2_n);
  and and_18 (and_18_out, Z_1_n, Z_2_n);
  and and_19 (and_19_out, Z_0_n, not_6_out, Z_2_n);
  and and_20 (and_20_out, not_7_out, Z_3_n);
  and and_21 (vGr, Z_1_n, Z_2_n);
  and and_22 (and_22_out, Z_0_n, not_6_out);
  and and_23 (and_23_out, Z_1_n, not_5_out);
  and and_24 (and_24_out, not_6_out, not_4_out);
  or or_2 (or_2_out, and_1_out, and_2_out);
  or or_3 (or_3_out, and_3_out, and_4_out, and_5_out, and_6_out);
  or or_4 (or_4_out, and_7_out, and_8_out, and_9_out);
  or or_5 (or_5_out, and_10_out, and_11_out, and_12_out);
  or or_6 (hGe, and_14_out, and_15_out);
  or or_7 (hR, and_17_out, and_18_out, Z_3_n);
  or or_8 (vGe, and_19_out, and_20_out);
  or or_9 (vR, and_22_out, and_23_out, and_24_out);
  D_FF u_Z_3_n (.D(or_2_out), .C(C), .Q(Z_3_n));  // open: nQ
  D_FF u_Z_2_n (.D(or_3_out), .C(C), .Q(Z_2_n));  // open: nQ
  D_FF u_Z_1_n (.D(or_4_out), .C(C), .Q(Z_1_n));  // open: nQ
  D_FF u_Z_0_n (.D(or_5_out), .C(C), .Q(Z_0_n));  // open: nQ
  // Probe test_Ampel_10_zustaende_komplett_C_geht nicht.fsm on {Z_3_n, Z_2_n, Z_1_n, Z_0_n}

  // Notes on the sheet:
  //   C: Hz: 2
endmodule
