// Digital circuit errorCircuit_red_too_long.dig as structural Verilog
module errorCircuit_red_too_long (
  output fGr,
  output fR,
  output hGe,
  output hGr,
  output hR,
  output vGe,
  output vGr,
  output vR
);

  // Probe state on 1'b0

  assign fGr = 1'b0;
  assign fR = 1'b1;
  assign hGe = 1'b0;
  assign hGr = 1'b1;
  assign hR = 1'b0;
  assign vGe = 1'b0;
  assign vGr = 1'b0;
  assign vR = 1'b1;
endmodule
