// Digital circuit errorCircuit_yellow_too_log.dig as structural Verilog
module errorCircuit_yellow_too_log (
  input  a,
  input  b,
  input  r,
  input  C,
  output fGr,
  output fR,
  output hGe,
  output hGr,
  output hR,
  output vGe,
  output vGr,
  output vR
);

  wire and_1_out, and_2_out, and_3_out, and_4_out, and_5_out, and_6_out, and_7_out, and_8_out, and_10_out,
       and_11_out, and_13_out, and_14_out, and_16_out, and_17_out, not_1_out, not_2_out, not_3_out,
       not_4_out, or_3_out, or_4_out, or_5_out, Z_0_n, Z_1_n, Z_2_n;

  not not_1 (not_1_out, r);
  not not_2 (not_2_out, Z_2_n);
  not not_3 (not_3_out, Z_1_n);
  not not_4 (not_4_out, Z_0_n);
  and and_1 (and_1_out, Z_0_n, Z_1_n, not_1_out);
  and and_2 (and_2_out, not_4_out, Z_2_n, not_1_out);
  and and_3 (and_3_out, Z_0_n, not_3_out, not_2_out, not_1_out);
  and and_4 (and_4_out, not_4_out, Z_1_n, not_1_out);
  and and_5 (and_5_out, not_4_out, not_3_out, not_2_out, b);
  and and_6 (and_6_out, not_4_out, not_3_out, not_2_out, a);
  and and_7 (and_7_out, not_4_out, Z_1_n, not_1_out);
  and and_8 (and_8_out, not_4_out, Z_2_n, not_1_out);
  and and_9 (fGr, Z_0_n, Z_1_n);
  or or_1 (fR, not_4_out, not_3_out);
  and and_10 (and_10_out, Z_0_n, not_3_out);
  and and_11 (and_11_out, not_4_out, Z_1_n);
  and and_12 (hGr, not_4_out, not_3_out, not_2_out);
  or or_2 (hR, Z_1_n, Z_2_n);
  and and_13 (and_13_out, not_4_out, Z_1_n);
  and and_14 (and_14_out, not_4_out, Z_2_n);
  and and_15 (vGr, Z_0_n, Z_1_n);
  and and_16 (and_16_out, Z_0_n, not_3_out);
  and and_17 (and_17_out, not_4_out, not_2_out);
  or or_3 (or_3_out, and_1_out, and_2_out);
  or or_4 (or_4_out, and_3_out, and_4_out);
  or or_5 (or_5_out, and_5_out, and_6_out, and_7_out, and_8_out);
  or or_6 (hGe, and_10_out, and_11_out);
  or or_7 (vGe, and_13_out, and_14_out);
  or or_8 (vR, and_16_out, and_17_out);
  D_FF u_Z_2_n (.D(or_3_out), .C(C), .Q(Z_2_n));  // open: nQ
  D_FF u_Z_1_n (.D(or_4_out), .C(C), .Q(Z_1_n));  // open: nQ
  D_FF u_Z_0_n (.D(or_5_out), .C(C), .Q(Z_0_n));  // open: nQ
  // Probe testautomaton_6_states.fsm on {Z_2_n, Z_1_n, Z_0_n}

  // Notes on the sheet:
  //   C: Hz: 2
endmodule
